// Logisim project multi4.circ as structural Verilog: 5 circuits, main circuit main
module main (
  input  [8:0] mul1,
  input  reset,
  input  [8:0] mul2,
  output [16:0] multiply_out
);

  wire a_1_out_one, clock_1_out, cnt_1_stop, multiplexer_1_out, multiplexer_2_out, not_1_out, q_1_out_one;
  wire [7:0] adder_1_out, multiplexer_3_out, x_1_out_eight;

  Clock clock_1 (.out(clock_1_out));
  not not_1 (not_1_out, reset);
  cnt cnt_1 (.clk(clock_1_out), .clear(reset), .stop(cnt_1_stop));
  Multiplexer multiplexer_1 (.in0(clock_1_out), .in1(1'b1), .out(multiplexer_1_out), .sel(cnt_1_stop));
  Adder adder_1 (.a(multiply_out[7:0]), .b(x_1_out_eight), .out(adder_1_out));  // open: cin, cout
  X x_1 (.in_eight(mul2[7:0]), .clk(clock_1_out), .out_eight(x_1_out_eight));
  Multiplexer multiplexer_2 (.in0(clock_1_out), .in1(1'b1), .out(multiplexer_2_out), .sel(cnt_1_stop));
  Q q_1 (
    .in_eight(multiplexer_3_out), .clk(multiplexer_1_out), .is_run(not_1_out), .out_one(q_1_out_one),
    .out_eight(multiply_out[7:0]));
  Multiplexer #(.width(8)) multiplexer_3 (
    .in0(multiply_out[7:0]), .in1(adder_1_out), .out(multiplexer_3_out), .sel(a_1_out_one));
  Hex_Digit_Display hex_digit_display_1 (.value(multiply_out[7:4]));  // open: dp
  xor xor_1 (multiply_out[16], mul2[8], mul1[8]);
  Hex_Digit_Display hex_digit_display_2 (.value(multiply_out[3:0]));  // open: dp
  Hex_Digit_Display hex_digit_display_3 (.value(multiply_out[15:12]));  // open: dp
  Hex_Digit_Display hex_digit_display_4 (.value(multiply_out[11:8]));  // open: dp
  A a_1 (
    .initial_eight(mul1[7:0]), .in_one(q_1_out_one), .is_run(not_1_out), .clk(multiplexer_2_out),
    .out_one(a_1_out_one), .out_eight(multiply_out[15:8]));
endmodule

module Q (
  input  [7:0] in_eight,
  input  clk,
  input  is_run,
  output out_one,
  output [7:0] out_eight
);

  wire [7:0] multiplexer_1_out;

  Multiplexer #(.width(8)) multiplexer_1 (.in0({8{1'b0}}), .in1(in_eight), .out(multiplexer_1_out), .sel(is_run));
  Register register_1 (.D(multiplexer_1_out), .en(1'b1), .clk(clk), .Q({out_eight[6:0], out_one}));  // open: clr

  assign out_eight[7] = 1'b0;
endmodule

module X (
  input  [7:0] in_eight,
  input  clk,
  output [7:0] out_eight
);

  Register register_1 (.D(in_eight), .en(1'b1), .clk(clk), .Q(out_eight));  // open: clr
endmodule

module A (
  input  [7:0] initial_eight,
  input  in_one,
  input  is_run,
  input  clk,
  output out_one,
  output [7:0] out_eight
);

  wire [7:0] multiplexer_1_out;

  Multiplexer #(.width(8)) multiplexer_1 (
    .in0(initial_eight), .in1({in_one, out_eight[7:1]}), .out(multiplexer_1_out), .sel(is_run));
  Register Q (.D(multiplexer_1_out), .en(1'b1), .clk(clk), .Q(out_eight));  // open: clr

  assign out_one = out_eight[0];
endmodule

module cnt (
  input  clk,
  input  clear,
  output stop
);

  wire [3:0] adder_1_out, multiplexer_1_out, multiplexer_2_out, register_1_q;

  Register #(.width(4)) register_1 (.D(multiplexer_1_out), .en(1'b1), .clk(clk), .Q(register_1_q));  // open: clr
  Multiplexer #(.width(4)) multiplexer_1 (.in0(multiplexer_2_out), .in1(4'b0000), .out(multiplexer_1_out), .sel(clear));
  Adder #(.width(4)) adder_1 (.a(4'b0001), .b(register_1_q), .out(adder_1_out));  // open: cin, cout
  Comparator #(.width(4)) comparator_1 (.a(register_1_q), .b(4'b1001), .eq(stop));  // open: gt, lt
  Multiplexer #(.width(4)) multiplexer_2 (.in0(adder_1_out), .in1(4'b1001), .out(multiplexer_2_out), .sel(stop));
endmodule
